# Fritzing sketch Main Circuit (saved by Fritzing 0.9.9b)
breadboards: 1

parts:
  Raspberry_Pi_1 = Raspberry Pi 3 [part_number=RPI-3-V1.2]
  ADC1 = MCP3008 [package=dil16]
  U1 = SLIDER [package=slider]
  U2 = SLIDER [package=slider]
  U3 = SLIDER [package=slider]
  U4 = SLIDER [package=slider]
  U5 = SLIDER [package=slider]
  U6 = SLIDER [package=slider]
  D1 = Diode [package=diode-1n4148]
  D2 = Diode [package=diode-1n4148]
  D3 = Diode [package=diode-1n4148]
  D4 = Diode [package=diode-1n4148]
  D5 = Diode [package=diode-1n4148]
  D6 = Diode [package=diode-1n4148]
  D7 = Diode [package=diode-1n4148]
  D8 = Diode [package=diode-1n4148]
  U9 = MODIFIED BUTTONPAD-2X2 [package=buttonpad-2x2-special]
  U10 = MODIFIED BUTTONPAD-2X2 [package=buttonpad-2x2-special]

nets:
  3.3V: Raspberry_Pi_1.3v3, Raspberry_Pi_1.3V3, ADC1.VREF, ADC1.VDD, U1.E, U2.E, U3.E, U4.E, U5.E, U6.E
  SPI MOSI: Raspberry_Pi_1.GIPO10, ADC1.Din
  SPI MISO: Raspberry_Pi_1.GIPO9, ADC1.Dout
  SPI CLK: Raspberry_Pi_1.GIPO11, ADC1.CLK
  GND: Raspberry_Pi_1.GND, ADC1.DGND, ADC1.AGND, U1.A, U2.A, U3.A, U4.A, U5.A, U6.A
  Loop Switch 2: Raspberry_Pi_1.GIPO21, U9.-C3_SIG1, U9.-C4_SIG1, U10.-C3_SIG1, U10.-C4_SIG1
  Loop Switch 1: Raspberry_Pi_1.GIPO20, U9.-C1_SIG1, U9.-C2_SIG1, U10.-C1_SIG1, U10.-C2_SIG1
  SPI CE0: Raspberry_Pi_1.GIPO8, ADC1.CS/SHDN
  5V: Raspberry_Pi_1.5V
  N1: ADC1.CH2, U5.S
  N2: ADC1.CH3, U4.S
  N3: ADC1.CH4, U6.S
  N4: ADC1.CH5, U3.S
  N5: ADC1.CH6, U2.S
  N6: ADC1.CH7, U1.S
  N7: D1.A, U9.-C1_SIG2
  Loop Switch GND A: D1.C, D2.C
  N8: D2.A, U9.-C3_SIG2
  N9: D3.A, U9.-C2_SIG2
  Loop Switch GND B: D3.C, D4.C
  N10: D4.A, U9.-C4_SIG2
  N11: D5.A, U10.-C1_SIG2
  Loop Switch GND C: D5.C, D8.C
  N12: D6.A, U10.-C4_SIG2
  Loop Switch GND D: D6.C, D7.C
  N13: D7.A, U10.-C2_SIG2
  N14: D8.A, U10.-C3_SIG2

notes:
  bass  |  mid  |  trebel
  EQ
  ________________________________________________
  distortion  |  reverb  |  compression
  Loop Pad
  Effects Sliders
